// Logisim project logisim2.circ as structural Verilog: 1 circuit, main circuit main
module main (
  input  A0,
  input  A1,
  input  A2,
  input  A3,
  input  A4,
  input  A5,
  input  A6,
  output Z,
  output E,
  output G,
  output L,
  output I,
  output O3,
  output O2,
  output O1,
  output O0
);

  wire and_1_out, and_2_out, and_3_out, and_4_out, and_5_out, and_6_out, and_7_out, and_8_out, and_9_out,
       and_10_out, and_11_out, and_12_out, and_13_out, and_14_out, and_15_out, and_16_out, and_17_out,
       and_18_out, and_19_out, and_20_out, and_21_out, and_22_out, and_23_out, and_24_out, and_25_out,
       and_26_out, and_27_out, and_28_out, and_29_out, and_30_out, and_31_out, and_32_out, and_33_out,
       and_34_out, and_35_out, and_36_out, and_37_out, and_38_out, and_39_out, and_40_out, and_41_out,
       and_42_out, and_43_out, and_44_out, and_45_out, and_46_out, and_47_out, and_48_out, and_49_out,
       and_50_out, and_51_out, and_52_out, and_53_out, and_54_out, and_55_out, and_56_out, and_57_out,
       and_59_out, and_60_out, and_61_out, and_62_out, and_63_out, and_64_out, and_65_out, and_66_out,
       and_67_out, and_68_out, and_69_out, and_70_out, n3_to_8_decoder_74138_1_p7,
       n3_to_8_decoder_74138_1_p8, n3_to_8_decoder_74138_1_p9, n3_to_8_decoder_74138_1_p10,
       n3_to_8_decoder_74138_1_p11, n3_to_8_decoder_74138_1_p12, n3_to_8_decoder_74138_1_p13,
       n3_to_8_decoder_74138_1_p14, nor_1_out, not_1_out, not_2_out, not_3_out, not_4_out, not_5_out,
       not_6_out, not_7_out, not_8_out, not_9_out, not_10_out, not_11_out, not_12_out, not_13_out,
       not_14_out, not_15_out, not_16_out, not_17_out, not_18_out, not_19_out, not_20_out, or_1_out,
       or_2_out, or_3_out, or_4_out, or_5_out, or_6_out, or_7_out, or_8_out, or_9_out, or_10_out, or_11_out,
       or_12_out, or_13_out, or_14_out, or_15_out, or_16_out, or_17_out, or_18_out, or_19_out, or_20_out,
       or_21_out, or_22_out, or_24_out, or_25_out, or_27_out, or_30_out, or_32_out, or_33_out, or_34_out,
       or_35_out, xor_1_out, xor_2_out, xor_3_out, xor_4_out, xor_5_out, xor_6_out, xor_7_out, xor_8_out,
       xor_9_out, xor_10_out, xor_11_out, xor_12_out, xor_13_out, xor_14_out;

  xor xor_1 (xor_1_out, A0, A2);
  and and_1 (and_1_out, A0, A3);
  or or_1 (or_1_out, and_34_out, xor_2_out);
  or or_2 (or_2_out, xor_1_out, xor_4_out);
  xor xor_2 (xor_2_out, and_7_out, and_1_out);
  and and_2 (and_2_out, and_7_out, and_1_out);
  and and_3 (and_3_out, not_6_out, A1);
  and and_4 (and_4_out, A3, not_3_out);
  and and_5 (and_5_out, A3, not_4_out);
  or or_3 (or_3_out, or_1_out, or_4_out);
  not not_1 (not_1_out, or_3_out);
  not not_2 (not_2_out, or_2_out);
  and and_6 (and_6_out, and_2_out, and_30_out);
  xor xor_3 (xor_3_out, and_2_out, and_30_out);
  xor xor_4 (xor_4_out, A3, A1);
  and and_7 (and_7_out, A1, A2);
  and and_8 (and_8_out, not_4_out, A3);
  and and_9 (and_9_out, not_6_out, A1);
  and and_10 (and_10_out, not_6_out, not_3_out);
  and and_11 (and_11_out, A2, and_4_out);
  or or_4 (or_4_out, and_6_out, xor_3_out);
  not not_3 (not_3_out, xor_4_out);
  and and_12 (and_12_out, A2, and_10_out);
  and and_13 (and_13_out, not_5_out, and_10_out);
  and and_14 (and_14_out, not_7_out, and_11_out);
  and and_15 (and_15_out, and_20_out, A2);
  xor xor_5 (xor_5_out, and_20_out, A2);
  and and_16 (and_16_out, A0, A1);
  not not_4 (not_4_out, A1);
  and and_17 (and_17_out, A2, A3);
  not not_5 (not_5_out, A2);
  not not_6 (not_6_out, A3);
  and and_18 (and_18_out, and_12_out, not_7_out);
  and and_19 (and_19_out, A0, and_13_out);
  not not_7 (not_7_out, A0);
  and and_20 (and_20_out, A0, A1);
  xor xor_6 (xor_6_out, and_15_out, A3);
  and and_21 (and_21_out, not_5_out, and_4_out);
  or or_5 (or_5_out, and_5_out, and_19_out);
  or or_6 (or_6_out, or_5_out, and_14_out);
  and and_22 (and_22_out, and_16_out, and_17_out);
  or or_7 (or_7_out, and_3_out, and_18_out);
  and and_23 (and_23_out, and_21_out, A0);
  xor xor_7 (xor_7_out, A1, A3);
  xor xor_8 (xor_8_out, A0, A2);
  and and_24 (and_24_out, not_5_out, not_6_out);
  and and_25 (and_25_out, A2, not_6_out);
  and and_26 (and_26_out, not_5_out, A3);
  and and_27 (and_27_out, A2, A3);
  and and_28 (and_28_out, not_5_out, not_6_out);
  and and_29 (and_29_out, not_7_out, not_4_out);
  or or_8 (or_8_out, or_7_out, and_23_out);
  not not_8 (not_8_out, xor_12_out);
  xor xor_9 (xor_9_out, A0, A1);
  xor xor_10 (xor_10_out, A1, A2);
  xor xor_11 (xor_11_out, A2, A3);
  and and_30 (and_30_out, A1, A3);
  xor xor_12 (xor_12_out, A1, A3);
  not not_9 (not_9_out, xor_7_out);
  not not_10 (not_10_out, xor_8_out);
  and and_31 (and_31_out, and_28_out, and_29_out);
  and and_32 (and_32_out, not_5_out, not_8_out);
  and and_33 (and_33_out, not_8_out, A2);
  xor xor_13 (xor_13_out, A0, A2);
  and and_34 (and_34_out, A2, A0);
  or or_9 (or_9_out, xor_13_out, xor_12_out);
  nor nor_1 (nor_1_out, not_9_out, not_10_out);
  and and_35 (and_35_out, A0, and_32_out);
  and and_36 (and_36_out, and_33_out, not_7_out);
  not not_11 (not_11_out, or_9_out);
  or or_10 (or_10_out, and_9_out, and_35_out);
  or or_11 (or_11_out, and_8_out, and_36_out);
  xor xor_14 (xor_14_out, and_34_out, xor_12_out);
  and and_37 (and_37_out, and_34_out, xor_12_out);
  or or_12 (or_12_out, xor_13_out, xor_14_out);
  and and_38 (and_38_out, xor_9_out, not_19_out);
  and and_39 (and_39_out, xor_10_out, not_19_out);
  and and_40 (and_40_out, xor_11_out, not_19_out);
  and and_41 (and_41_out, A3, not_19_out);
  // _3_to_8_decoder__74138 #(.Facing("east")) 3_to_8_decoder_74138_1: pin names not known; wires that end beside it: A4, A5, A6, 1'b1, 1'b0, 1'b0, n3_to_8_decoder_74138_1_p7, n3_to_8_decoder_74138_1_p8, n3_to_8_decoder_74138_1_p9, n3_to_8_decoder_74138_1_p10, n3_to_8_decoder_74138_1_p11, n3_to_8_decoder_74138_1_p12, n3_to_8_decoder_74138_1_p13, n3_to_8_decoder_74138_1_p14
  and and_42 (and_42_out, not_16_out, and_24_out);
  and and_43 (and_43_out, not_16_out, and_25_out);
  and and_44 (and_44_out, not_16_out, and_26_out);
  and and_45 (and_45_out, not_16_out, and_27_out);
  and and_46 (and_46_out, not_16_out, and_31_out);
  or or_13 (or_13_out, and_37_out, and_30_out);
  or or_14 (or_14_out, and_54_out, and_42_out);
  or or_15 (or_15_out, or_12_out, or_13_out);
  not not_12 (not_12_out, n3_to_8_decoder_74138_1_p7);
  not not_13 (not_13_out, n3_to_8_decoder_74138_1_p8);
  not not_14 (not_14_out, n3_to_8_decoder_74138_1_p9);
  not not_15 (not_15_out, n3_to_8_decoder_74138_1_p10);
  not not_16 (not_16_out, n3_to_8_decoder_74138_1_p11);
  not not_17 (not_17_out, n3_to_8_decoder_74138_1_p12);
  not not_18 (not_18_out, n3_to_8_decoder_74138_1_p13);
  not not_19 (not_19_out, n3_to_8_decoder_74138_1_p14);
  or or_16 (or_16_out, and_55_out, and_43_out);
  or or_17 (or_17_out, and_52_out, or_14_out);
  not not_20 (not_20_out, or_15_out);
  or or_18 (or_18_out, and_57_out, and_45_out);
  or or_19 (or_19_out, and_51_out, or_16_out);
  or or_20 (or_20_out, and_38_out, or_17_out);
  and and_47 (and_47_out, xor_13_out, not_12_out);
  and and_48 (and_48_out, xor_14_out, not_12_out);
  and and_49 (and_49_out, or_13_out, not_12_out);
  and and_50 (and_50_out, not_20_out, not_12_out);
  and and_51 (and_51_out, not_9_out, not_15_out);
  and and_52 (and_52_out, not_10_out, not_15_out);
  and and_53 (and_53_out, nor_1_out, not_15_out);
  or or_21 (or_21_out, and_69_out, or_18_out);
  or or_22 (or_22_out, and_39_out, or_19_out);
  or or_23 (O3, and_41_out, or_21_out);
  or or_24 (or_24_out, and_48_out, or_22_out);
  and and_54 (and_54_out, not_14_out, not_7_out);
  and and_55 (and_55_out, not_14_out, xor_9_out);
  and and_56 (and_56_out, not_14_out, xor_5_out);
  and and_57 (and_57_out, not_14_out, xor_6_out);
  and and_58 (I, not_14_out, and_22_out);
  and and_59 (and_59_out, not_14_out, and_22_out);
  and and_60 (and_60_out, not_2_out, not_18_out);
  and and_61 (and_61_out, or_8_out, not_18_out);
  and and_62 (and_62_out, or_6_out, not_18_out);
  and and_63 (and_63_out, not_13_out, or_10_out);
  and and_64 (and_64_out, not_13_out, or_11_out);
  and and_65 (and_65_out, not_13_out, not_11_out);
  or or_25 (or_25_out, and_49_out, and_56_out);
  or or_26 (E, and_65_out, and_60_out);
  or or_27 (or_27_out, or_25_out, and_44_out);
  and and_66 (and_66_out, not_17_out, and_34_out);
  and and_67 (and_67_out, not_17_out, xor_2_out);
  and and_68 (and_68_out, not_17_out, xor_3_out);
  and and_69 (and_69_out, not_17_out, and_6_out);
  and and_70 (and_70_out, not_17_out, not_1_out);
  or or_28 (G, and_64_out, and_61_out);
  or or_29 (O1, and_67_out, or_24_out);
  or or_30 (or_30_out, and_47_out, or_20_out);
  or or_31 (L, and_63_out, and_62_out);
  or or_32 (or_32_out, and_50_out, and_59_out);
  or or_33 (or_33_out, and_68_out, or_27_out);
  or or_34 (or_34_out, or_32_out, and_53_out);
  or or_35 (or_35_out, or_34_out, and_46_out);
  or or_36 (O2, and_40_out, or_33_out);
  or or_37 (O0, and_66_out, or_30_out);
  or or_38 (Z, and_70_out, or_35_out);

  // Notes on the sheet:
  //   t1
  //   md
  //   P10
  //   tc
  //   l_sign
  //   t1
  //   mul01
  //   mulcarry
  //   g_sign
  //   tg
  //   mulZ
  //   t3
  //   scmpE
  //   mul03
  //   t2
  //   mul02
  //   sd
  //   same_sign
  //   P01
  //   g1
  //   l1
  //   ta
  //   te
  //   th
  //   tb
  //   tf
  //   l_neg
  //   incO0
  //   nA0
  //   carry2
  //   incO2
  //   t2
  //   nA1
  //   t1
  //   nA2
  //   nA3
  //   g_pos
  //   l_pos
  //   carry1
  //   incI
  //   incO3
  //   td
  //   scmpL
  //   t3
  //   t2
  //   g_neg
  //   grayO0-2
  //   incO1
  //   carry1b
  //   bit1_temp
  //   d1
  //   xnor1-0_temp
  //   range_O0-3
  //   t1 t2
  //   scmpG
  //   eq_msb
  //   P11
  //   xnorO1-0
  //   rangeZ
  //   t2
  //   t1
  //   d0
  //   adadO0 carry0
  //   mul00
  //   P00
  //   t1
  //   ucmpE
  //   xnorZ
  //   l0
  //   g0
  //   ucmpL
  //   ucmpG
  //   addO1
  //   carry1a
  //   t1
  //   op7_O0-3
  //   op4_O0-3,Z
  //   t2
  //   addO2
  //   op0-7
  //   addZ
  //   op0_O0-2,Z
  //   op3_o1-0-Z
  //   op2_O0-3,I,Z
  //   op6_E
  //   op6_G
  //   op1_L
  //   op1_G
  //   op1_E
  //   op6_L
  //   op5_O0-3,Z
  //   t1
  //   t2
  //   t3
endmodule
